# Fritzing sketch Arduino_Wecker (saved by Fritzing 0.9.3b)
breadboards: 1

parts:
  LCM1602_IIC1 = LCM1602 IIC [part_number="LCM1602 IIC" chip_label="LCM1602 IIC" package="DIP (Dual Inline) [THT]"]
  DHT1 = DHT22 Humidity and Temperature Sensor
  U1 = mystery part, 4 pins [chip_label=Piezo]
  Photo = Photocell (LDR) [package=THT]  # not connected
  S1 = Pushbutton [package="[THT]"]
  S2 = Pushbutton [package="[THT]"]
  S3 = Pushbutton [package="[THT]"]
  S4 = Pushbutton [package="[THT]"]
  R2 = Resistor [tolerance=±5% resistance=220 package=THT]
  R3 = Resistor [tolerance=±5% resistance=10k package=THT]
  R4 = Resistor [tolerance=±5% resistance=10k package=THT]
  R5 = Resistor [tolerance=±5% resistance=10k package=THT]
  R6 = Resistor [tolerance=±5% resistance=10k package=THT]
  R7 = Resistor [tolerance=±5% resistance=1k package=THT]
  ZS-042_RTC1 = ZS-042 RTC Module
  Arduino_Nano = Arduino Nano (Rev3.0)
  J4 = female pin header, 5 pins [form="♀ (female)"]
  RE1 = Rotary Encoder [package=THT]
  J5 = female pin header, 4 pins [form="♀ (female)"]
  U2 = mystery part, 4 pins [chip_label=7-Segment]
  T1 = LM35 Temperature Sensor [package="TO92 [THT]"]
  J6 = female pin header, 3 pins [form="♀ (female)"]

nets:
  GND: LCM1602_IIC1.GND, DHT1.NULL, DHT1.GND, R2.Pin_1, R3.Pin_0, R4.Pin_0, R5.Pin_0, R6.Pin_0, R7.Pin_0, ZS-042_RTC1.GND, Arduino_Nano.GND, J4.pin5, RE1.EncoderPinA, J5.pin1, U2.pin4, T1.GND, J6.pin3
  VCC: LCM1602_IIC1.VCC, DHT1.VDD, S1.Pin_3, S1.Pin_4, S2.Pin_3, S2.Pin_4, S3.Pin_3, S3.Pin_4, S4.Pin_3, S4.Pin_4, ZS-042_RTC1.VCC, Arduino_Nano.5V, J4.pin4, RE1.EncoderPinB, J5.pin2, U2.pin3, T1.+Vs, J6.pin1
  N1: LCM1602_IIC1.SDA, ZS-042_RTC1.SDA, Arduino_Nano.A4, J4.pin3
  N2: LCM1602_IIC1.SCL, ZS-042_RTC1.SCL, Arduino_Nano.A5, J4.pin2
  N3: LCM1602_IIC1.LED_A, Arduino_Nano.D8, J4.pin1
  N4: DHT1.DATA, Arduino_Nano.D7
  N5: U1.pin1, U1.pin2, Arduino_Nano.D6
  N6: U1.pin3, U1.pin4, R2.Pin_0
  N7: S1.Pin_1, S1.Pin_2, R5.Pin_1, Arduino_Nano.D2
  N8: S2.Pin_1, S2.Pin_2, R4.Pin_1, Arduino_Nano.D3
  N9: S3.Pin_1, S3.Pin_2, R6.Pin_1, Arduino_Nano.D4
  N10: S4.Pin_1, S4.Pin_2, R3.Pin_1, Arduino_Nano.D5
  N11: R7.Pin_1, Arduino_Nano.A1
  N12: Arduino_Nano.D9, J5.pin4, U2.pin1
  N13: Arduino_Nano.D10, J5.pin3, U2.pin2
  N14: Arduino_Nano.A2, RE1.EncoderPinC
  N15: Arduino_Nano.A0, T1.Vout, J6.pin2

custom parts:
  LCM1602 IIC: I2C-Module to use a 1602 or 2004 LCD on with the wire.h libory Serial LCD Modul

// code stored in the sketch: Anzeige.ino
void anzeige() {



  if (analogRead(photo) > storage.hell) {
    display.setBrightness(0x00);//helligkeit auf maximum
    digitalWrite(lcdStrom, HIGH);
  } else {
    display.setBrightness(0x0f);//helligkeit auf maximum
    digitalWrite(lcdStrom, LOW);
  }




  display.showNumberDec(hour() * 100 + minute(), true);
  lcd.setCursor(0, 0);
  sprintf(lcdChar, "%2s;%2s;%2s;%2s;%2s;%2s;%2s", weckzeiten[0].getString(), weckzeiten[1].getString(), weckzeiten[2].getString(), weckzeiten[3].getString(), weckzeiten[4].getString(), weckzeiten[5].getString(), weckzeiten[6].getString());
  lcd.print(lcdChar);/**/
  switch (menuID) {
    case 0:
      if (rechts.checkPressed()) {
        subMenuID++;
        lastPot = analogRead(poti);
        lcd.clear();
      }
      if (links.checkPressed()) {
        subMenuID--;
        lastPot = analogRead(poti);
        lcd.clear();
      }
      if (menu.checkPressed()) {
        subMenuID = 0;
        lcd.clear();
      }
      lcd.setCursor(0, 1);/**/
      /*lcd.setCursor(0, 0); /**/
      printTime();
      lcd.setCursor(0, 2);/**/
      /*lcd.setCursor(0, 1); /**/
      subMenuMax(3);
      switch (subMenuID) {
        case 0:
          sprintf(lcdChar, "%3d %%; %2d%cC         ", int(dht.readHumidity()), int(dht.readTemperature()), char(223));
          lcd.print(lcdChar);
          break;
        case 1:
          lcd.print("Uhr einstellen      ");
          if (okay.checkPressed()) {
            menuID = 1;
            subMenuID = 0;
            tm.Hour = hour();
            tm.Minute = minute();
            tm.Day = day();
            tm.Month = month();
            tm.Year = CalendarYrToTm(year());
            lastPot = analogRead(poti);
            lcd.clear();
          }
          break;
        case 2:
          lcd.print("Weckzeiten          ");
          if (okay.checkPressed()) {
            menuID = 3;
            weckID = 0;
            lastPot = analogRead(poti);
            lcd.clear();
          }
          break;
        case 3:
          lcd.print("Einstellungen       ");
          if (okay.checkPressed()) {
            menuID = 5;
            weckID = 0;
            lastPot = analogRead(poti);
            lcd.clear();
            lastPot = storage.hell;
          }
          break;
          /*16:2lcd
            case 4:
            sprintf(lcdChar, "%2s;%2s;%2s;%2s;%2s;%2s;%2s", weckzeiten[0].getString(), weckzeiten[1].getString(), weckzeiten[2].getString(), weckzeiten[3].getString(), weckzeiten[4].getString(), weckzeiten[5].getString(), weckzeiten[6].getString());
            lcd.print(lcdChar);
            break;
          */

      }
      break;
    case 1:
      if (rechts.checkPressed()) {
        subMenuID++;
        lastPot = analogRead(poti);
        lcd.clear();
      }
      if (links.checkPressed()) {
        subMenuID--;
        lastPot = analogRead(poti);
        lcd.clear();
      }
      if (menu.checkPressed()) {
        menuID = 0;
        lcd.clear();
      }
      lcd.setCursor(0, 1);
      printTime();/**/
      subMenuMax(5);
      lcd.setCursor(0, 2);
      if (second() - secondOffset < 0) {
        secondNew = 60 + second() - secondOffset;
      } else {
        secondNew = second() - secondOffset;
      }
      switch (subMenuID) {
        case 0:
          if (lastPot > analogRead(poti) + 5 || lastPot < analogRead(poti) - 5) {
            tm.Hour = map(analogRead(poti), 0, 1024, 0, 24);
          }
          printTimeSet("Std");
          setNewTime();
          break;
        case 1:
          if (lastPot > analogRead(poti) + 5 || lastPot < analogRead(poti) - 5) {
            tm.Minute = map(analogRead(poti), 0, 1024, 0, 61);
          }
          printTimeSet("Min");
          setNewTime();
          break;
        case 2:
          if (okay.checkPressed()) {
            secondOffset = second();
          }
          printTimeSet("Sek");
          break;
        case 3:
          if (lastPot > analogRead(poti) + 5 || lastPot < analogRead(poti) - 5) {
            tm.Day = map(analogRead(poti), 0, 1024, 1, 32);
          }
          printTimeSet("Tag");
          setNewTime();
          break;
        case 4:
          if (lastPot > analogRead(poti) + 5 || lastPot < analogRead(poti) - 5) {
            tm.Month = map(analogRead(poti), 0, 1024, 1, 13);
          }
          printTimeSet("Mon");
          setNewTime();
          break;
        case 5:
          if (lastPot > analogRead(poti) + 5 || lastPot < analogRead(poti) - 5) {
            tm.Year = CalendarYrToTm(map(analogRead(poti), 0, 1024, 1999, 2051));
          }
          printTimeSet("Jah");
          setNewTime();
          break;
      }
      break;
    case 3:
      if (rechts.checkPressed()) {
        subMenuID++;
        lastPot = analogRead(poti);
        lcd.clear();
      }
      if (links.checkPressed()) {
        subMenuID--;
        lastPot = analogRead(poti);
        lcd.clear();
      }
      if (menu.checkPressed()) {
        menuID = 0;
        lcd.clear();
      }

      if (okay.checkPressed()) {
        weckID = subMenuID;
        menuID = 4;
        subMenuID = 0;
        weckStunde = weckzeiten[weckID].getHH();
        weckMinute = weckzeiten[weckID].getMM();
        if (weckzeiten[weckID].getActive()) {
          weckTag = weckzeiten[weckID].getWD();
        } else {
          weckTag = 10;
        }
        saveConfig();
      }
      subMenuMax(6);

      /*
        lcd.setCursor(0, 0);
        sprintf(lcdChar, "%2s;%2s;%2s;%2s;%2s;%2s;%2s", weckzeiten[0].getString(), weckzeiten[1].getString(), weckzeiten[2].getString(), weckzeiten[3].getString(), weckzeiten[4].getString(), weckzeiten[5].getString(), weckzeiten[6].getString());
        lcd.print(lcdChar);
      */
      lcd.setCursor(subMenuID * 3, 1);
      lcd.print("++");
      lcd.setCursor(0, 2);
      printTime();/**/

      break;
    case 4:
      if (rechts.checkPressed()) {
        subMenuID++;
        lastPot = analogRead(poti);
        lcd.clear();
      }
      if (links.checkPressed()) {
        subMenuID--;
        lastPot = analogRead(poti);
        lcd.clear();
      }
      if (menu.checkPressed()) {
        menuID = 3;
        lcd.clear();
      }
      subMenuMax(2);
      lcd.setCursor(weckID * 3, 1);
      lcd.print("++");
      lcd.setCursor(0, 2);
      printTime();/**/
      switch (subMenuID) {
        case 0:
          if (lastPot > analogRead(poti) + 5 || lastPot < analogRead(poti) - 5) {
            weckStunde = map(analogRead(poti), 0, 1024, 0, 24);
          }
          weckMen[0] = 'H';
          weckMen[1] = 'H';
          break;
        case 1:
          if (lastPot > analogRead(poti) + 5 || lastPot < analogRead(poti) - 5) {
            weckMinute = map(analogRead(poti), 0, 1024, 0, 60);
          }
          weckMen[0] = 'M';
          weckMen[1] = 'M';
          break;
        case 2:
          if (lastPot > analogRead(poti) + 5 || lastPot < analogRead(poti) - 5) {
            weckTag = map(analogRead(poti), 0, 1024, 0, weckzeiten[weckID].getDays());
          }
          weckMen[0] = 'D';
          weckMen[1] = 'A';
          break;
      }
      lcd.setCursor(0, 3);
      sprintf(lcdChar, "%02d:%02d %03s %02s", weckStunde, weckMinute, weckzeiten[weckID].createStr(weckTag), weckMen);
      lcd.print(lcdChar);
      if (okay.checkPressed()) {
        menuID = 3;
        lcd.clear();
        weckzeiten[weckID].setAlarm(weckStunde, weckMinute, weckTag);
        storage.weckZ[weckID] = weckzeiten[weckID].getInt();
        saveConfig();
      }
      break;
    case 5:
      lcd.setCursor(0, 1);
      printTime();
      lcd.setCursor(0, 2);
      sprintf(lcdChar, "%04d--%04d/%04d", lastPot, storage.hell, analogRead(photo));
      lcd.print(lcdChar);
      if (menu.checkPressed()) {
        menuID = 0;
        storage.hell = lastPot;
        lcd.clear();
      }
      storage.hell = analogRead(poti);
      if (okay.checkPressed()) {
        menuID = 0;
        saveConfig();
        lcd.clear();
      }

      break;

  }
}

// code stored in the sketch: sonstFunctions.ino
void subMenuMax(byte subMenuMax) {
  if (subMenuID > 254) {
    subMenuID = subMenuMax; //maximale zahl
  }
  if (subMenuID > subMenuMax) { // maximale subMenu zahl
    subMenuID = 0;
  }
}

void weckentest() {
  if (second() <= 2) {
    for (int i = 0; i < anzWeck; i++) {
      if (weckzeiten[i].getAlarm(hour(), minute(), weekday())) {
        wecken = 1;
      }
    }
  }
  if (okay.checkPressed()) {
    wecken = 0;
    saveConfig();
  }
}

bool softDelay(byte ID, int diff) {
  unsigned long nowMillis = millis();
  if (nowMillis < lastMillis[ID]) {
    lastMillis[ID] = nowMillis;
    return true;
  } else if (nowMillis >= lastMillis[ID] + diff) {
    lastMillis[ID] = nowMillis;
    return true;
  } else {
    return false;
  }
}

void loadConfig() {
  // To make sure there are settings, and they are YOURS!
  // If nothing is found it will use the default settings.
  if (EEPROM.read(CONFIG_START + 0) == CONFIG_VERSION[0] &&
      EEPROM.read(CONFIG_START + 1) == CONFIG_VERSION[1] &&
      EEPROM.read(CONFIG_START + 2) == CONFIG_VERSION[2])
    for (unsigned int t = 0; t < sizeof(storage); t++)
      *((char*)&storage + t) = EEPROM.read(CONFIG_START + t);
}

void saveConfig() {
  for (unsigned int t = 0; t < sizeof(storage); t++) {
    if (EEPROM.read(CONFIG_START + t) != *((char*)&storage + t)) {
      EEPROM.write(CONFIG_START + t, *((char*)&storage + t));
      Serial.print("w");
    } else {
      Serial.print("r");
    }
  }
  Serial.print("  ");
  Serial.print(sizeof(storage));
  Serial.println(" Bytes aktualisiert");
}

// code stored in the sketch: timeFunctions.ino
void printTimeSet(char const aktiv[3]) {
  sprintf(lcdChar, "neu:%02d:%02d:%02d %s", tm.Hour, tm.Minute, secondNew, aktiv);
  lcd.print(lcdChar);
  lcd.setCursor(0, 3);
  sprintf(lcdChar, "    %02d.%02d.%04d    ", tm.Day, tm.Month, tm.Year + 1970);
  lcd.print(lcdChar);
}

void setNewTime() {
  if (okay.checkPressed()) {
    tm.Second = (second() + 60 - secondOffset) % 60;
    t = makeTime(tm);
    RTC.set(t);
    setTime(t);
    lcd.clear();
    menuID = 0;
    secondOffset = 0;
  }
}

void printTime() {
  sprintf(lcdChar, " %02d:%02d:%02d %03s %02d.%02d.   ", hour(), minute(), second(), weckzeiten[0].createStr(weekday()), day(), month());
  lcd.print(lcdChar);
}

void sommerZeit() {
  bool DST = false;
  if (month() <= 2 || month() >= 11)
    DST = false;                                   // Winter months
  if (month() >= 4 && month() <= 9)
    DST = true;                                    // Summer months
  if (month() == 3 && (day() - (weekday() - 1)) >= 25) { // Begin of summer time
    if (hour() >= 2 || weekday() != 1)
      DST = true;
  }
  if (month() == 10 && day() - (weekday() - 1) < 25)
    DST = true;
  if (month() == 10 && day() - (weekday() - 1) >= 25) {
    if ((hour() >= 3) || weekday() != 1 || (hour() == 2 && !storage.sommer)) {
      DST = false;
    }
    else {
      DST = true;
    }
  }
  if (DST && !storage.sommer) {
    tm.Hour = hour() + 1;
    tm.Minute = minute();
    tm.Second = second();
    tm.Day = day();
    tm.Month = month();
    tm.Year = CalendarYrToTm(year());
    t = makeTime(tm);
    RTC.set(t);
    setTime(t);
    storage.sommer = true;
    saveConfig();
  } else if (!DST && storage.sommer) {
    tm.Hour = hour() - 1;
    tm.Minute = minute();
    tm.Second = second();
    tm.Day = day();
    tm.Month = month();
    tm.Year = CalendarYrToTm(year());
    t = makeTime(tm);
    RTC.set(t);
    setTime(t);
    storage.sommer = false;
    saveConfig();
  }

}

// code stored in the sketch: Wecken_T5.ino
//Bibliotheken:
#include <Wire.h> //F�r viele I2C: LCD;RTC;
#include <LiquidCrystal_I2C.h> //F�rs LCD
#include <Time.h> //Zeitverwaltung
#include <DS3232RTC.h> //RTC
#include <stdio.h> //f�r formatierte charArrays
#include <DHT.h> //Feuchte und temperatursensor
#include <Pingoin.h> //Eigene Objektsammlung
#include <EEPROM.h> //speichern im konsistenten speicher
#include <TM1637Display.h> //7Segment display


//Pinnbelegung:
#define poti A2
#define tSensor A0
#define photo A1
#define lcdSpalten 20
#define lcdZeilen 4
#define DHTPIN 7
#define DHTTYPE DHT22
#define klingel 6
#define anzWeck 7
#define lcdStrom 8
#define CLK 9
#define DIO 10
#define CONFIG_VERSION "001"
#define CONFIG_START 64

struct StoreStruct {
  // This is for mere detection if they are your settings
  char version[4];
  int weckZ[7];
  int hell;
  bool sommer;
} storage = {
  CONFIG_VERSION,
  {0, 0, 0, 0, 0, 0, 0},
  100,
  false
};


//Buttons:
PingoButton links(2);
PingoButton rechts(3);
PingoButton menu(4);
PingoButton okay(5);

//laufzeitvariablen:
byte menuID = 0; //Position im Menu 0:=Anzeige
byte subMenuID = 0;
byte secondOffset = 0;
byte secondNew = 0;
tmElements_t tm;
time_t t;
char lcdChar [lcdSpalten]; //String zum Anzeigen, wird f�r formatierte Ausgaben ben�tigt
bool wecken = 0;
bool blinken = 0;
AlarmTime weckzeiten[anzWeck];
short int lastPot = 0;
byte weckStunde = 0;
byte weckMinute = 0;
byte weckTag = 0;
byte weckID = 0;
char weckMen[3] = "hh";
unsigned long lastMillis[] = {0}; //Laufzeiten f�r soft delay
//Blinken,


//Ger�te:
LiquidCrystal_I2C lcd(0x27, lcdSpalten, lcdZeilen);//Definition des LCD displays
DHT dht(DHTPIN, DHTTYPE); //Feuchte und Temperatur
TM1637Display display(CLK, DIO);

void setup() {
  //ger�te:
  Serial.begin(9600); //Serieller Monitor
  lcd.begin(); //Initialisierung des LCDs
  lcd.clear(); //auf jeden fall mit leerer LCD starten
  setSyncProvider(RTC.get);//Zeit wird regelm��ig mit RTC synchronisiert

  //Pins:
  pinMode(lcdStrom, OUTPUT);
  digitalWrite(13, LOW);
  //�berpr�fungen:
  if (timeStatus() != timeSet)
    Serial.println("Konnte nicht mit der RTC verbinden");
  else
    Serial.println("Zeit wurde mit RTC synchronisiert");

  //Einstellungen laden
  loadConfig();
  for (int i = 0; i < 7; i++) {
    weckzeiten[i].setInt(storage.weckZ[i]);
  }
}

void loop() {
  sommerZeit();
  weckentest();
  anzeige();  //Menus anzeigen und Funktionen ausf�hren
  klingeln(); //Klingelhandler
}

void klingeln() {
  if (softDelay(0, 500)) {
    if (wecken && blinken) {
      tone(klingel, 666, 500);
    } else {
      if (wecken) blinken = !blinken;
      digitalWrite(klingel, LOW);
    }
  }
}
